# Fritzing sketch schematic (saved by Fritzing 1.0.0rc)
breadboards: 1

parts:
  OLED_I2C1 = OLED 128x64 I2C Monochrome Display
  Mod1 = Amica NodeMCU DEVKIT 1.0
  E3Z-R61 = E18-D80NK_1 [mn=or mpn=E3Z-LAS-R8 part_number="(NPN NO)" package=THT]
  Mod2 = Passive Buzzer
  S1 = Pushbutton [package="[THT]"]
  R1 = Resistor [tolerance=±5% resistance=10k package="0402 [SMD]"]

nets:
  N1: OLED_I2C1.SDA, Mod1.pin_14
  N2: OLED_I2C1.SCK, Mod1.pin_13
  N3: OLED_I2C1.VDD, E3Z-R61.pin2, Mod2.S
  N4: OLED_I2C1.GND, E3Z-R61.pin1, Mod2.-
  N5: Mod1.pin1, Mod1.pin_10, Mod1.pin_26
  N6: Mod1.pin2, Mod1.pin_9, Mod1.pin_25, Mod1.pin_29
  N7: Mod1.pin4, E3Z-R61.pin3
  N8: Mod1.pin6, Mod2.NC
  N9: Mod1.pin8, S1.Pin_3, S1.Pin_4, R1.Pin_1
  N10: S1.Pin_1, S1.Pin_2

custom parts:
  E18-D80NK_1: E18-D80NK Proximity Sensor module.
