# Fritzing sketch schematic2 (saved by Fritzing 1.0.0rc)
breadboards: 1

parts:
  I2C_SSD1315_128x64 = OLED 128x64 I2C Monochrome Display
  E3Z-R61 = E18-D80NK_1 [mn=or part_number="(NPN NO)" mpn=E3Z-LAS-R8 package=THT]
  Mod2 = Passive Buzzer
  S1 = Pushbutton [package="[THT]"]
  R1 = Resistor [tolerance=±5% resistance=10k package="0402 [SMD]"]
  WeMos_D1_Mini1 = WeMos D1 Mini  # not connected

nets:
  N1: I2C_SSD1315_128x64.VDD, R1.Pin_1
  N2: I2C_SSD1315_128x64.GND, E3Z-R61.pin1, Mod2.-, S1.Pin_1, S1.Pin_2
  N3: E3Z-R61.pin2, Mod2.S
  N4: S1.Pin_3, S1.Pin_4

notes:
  +3V
  GND
  +5V
  You can power the entire board either through the MicroUSB port on the Wemos module or via the 5V and G (GND) pins.

custom parts:
  E18-D80NK_1: E18-D80NK Proximity Sensor module.
